// Logisim project Ctl_Data_Processing.circ as structural Verilog: 2 circuits, main circuit Data_Processing
module Data_Processing (
  input  Enable,
  input  [15:0] Instruction,
  output [2:0] Rd,
  output [2:0] Rn,
  output [2:0] Rm,
  output [3:0] ALU_Opcode,
  output [3:0] Flags_Update_Mask
);

  wire [3:0] tableauverite_1_v;

  TableauVerite tableauverite_1 (
    .operateur(Instruction[9:6]), .N(tableauverite_1_v[3]), .Z(tableauverite_1_v[2]),
    .C(tableauverite_1_v[1]), .V(tableauverite_1_v[0]));
  Multiplexer #(.enable("false"), .width(3)) multiplexer_1 (
    .in0(3'b000), .in1(Instruction[2:0]), .out(Rd), .sel(Enable));
  Multiplexer #(.enable("false"), .width(3)) multiplexer_2 (
    .in0(3'b000), .in1(Instruction[2:0]), .out(Rn), .sel(Enable));
  Multiplexer #(.enable("false"), .width(3)) multiplexer_3 (
    .in0(3'b000), .in1(Instruction[5:3]), .out(Rm), .sel(Enable));
  Multiplexer #(.enable("false"), .width(4)) multiplexer_4 (
    .in0(4'b0000), .in1(Instruction[9:6]), .out(ALU_Opcode), .sel(Enable));
  Multiplexer #(.enable("false"), .width(4)) multiplexer_5 (
    .in0(4'b0000), .in1(tableauverite_1_v), .out(Flags_Update_Mask), .sel(Enable));

  // Notes on the sheet:
  //   Note 2: RSB instruction has Rn as 1st operand.
  //   MUL instruction has Rn as 1st operand and Rdm as 2nd operand
  //   For simplification purposes, Rm is used for 1st operand both here and in the ALU.
  //   Note: instructions that does not save the result will still have the second operand as the destination register, the ALU will copy the second register to the destination register
  //   Pull output low on Enable = 0
endmodule

module TableauVerite (
  input  [3:0] operateur,
  output N,
  output Z,
  output C,
  output V
);

  wire and_1_out, and_2_out, and_3_out, and_4_out, and_5_out, not_1_out, not_2_out, not_3_out, not_4_out;

  not not_1 (not_1_out, operateur[3]);
  not not_2 (not_2_out, operateur[2]);
  not not_3 (not_3_out, operateur[1]);
  not not_4 (not_4_out, operateur[0]);
  and and_1 (and_1_out, not_2_out, operateur[1]);
  or or_1 (C, and_1_out, and_2_out);
  and and_2 (and_2_out, not_1_out, operateur[2]);
  and and_3 (and_3_out, not_1_out, operateur[2], not_3_out, operateur[0]);
  and and_4 (and_4_out, not_1_out, operateur[2], operateur[1], not_4_out);
  or or_2 (V, and_3_out, and_4_out, and_5_out);
  and and_5 (and_5_out, operateur[3], not_2_out, operateur[1]);

  assign N = 1'b1;
  assign Z = 1'b1;
endmodule
