// Logisim project Ctl_Shift_Add_Sub_Mov.circ as structural Verilog: 2 circuits, main circuit flags_table
module Shift_Add_Sub_Mov (
  input  Enable,
  input  [15:0] Instruction,
  output [3:0] Flags_Update_Mask,
  output Carry,
  output Imm32_Enable,
  output [2:0] Rm,
  output [2:0] Rn,
  output [2:0] Rd,
  output [4:0] Imm5,
  output [31:0] Imm32,
  output [3:0] ALU_Opcode
);

  wire and_1_out, and_2_out, and_3_out, comparator_1_eq, comparator_2_gt, comparator_3_eq, or_1_out;
  wire [2:0] multiplexer_1_out, multiplexer_4_out;
  wire [3:0] adder_1_out, adder_2_out, adder_3_out, flags_table_1_flags, multiplexer_3_out,
       multiplexer_5_out, multiplexer_6_out;
  wire [4:0] bitselector_2_out;
  wire [8:0] bitselector_1_out;
  wire [31:0] bit_extender_1_out, bit_extender_2_out, multiplexer_2_out, multiplexer_7_out, negator_1_out;

  BitSelector #(.group(9), .width(16)) bitselector_1 (.in(Instruction), .out(bitselector_1_out), .sel(1'b1));
  BitSelector #(.group(5), .width(9)) bitselector_2 (.in(bitselector_1_out), .out(bitselector_2_out), .sel(1'b0));
  assign bit_extender_1_out = {{24{1'b0}}, Instruction[7:0]};  // Bit_Extender bit_extender_1
  Adder #(.width(4)) adder_1 (.a(4'b0010), .b(Instruction[14:11]), .out(adder_1_out));  // open: cin, cout
  and and_1 (and_1_out, ~Instruction[11], ~Instruction[12]);  // AND_Gate
  assign bit_extender_2_out = {{29{1'b0}}, Instruction[8:6]};  // Bit_Extender bit_extender_2
  Negator #(.width(32)) negator_1 (.in(bit_extender_1_out), .out(negator_1_out));
  Comparator #(.mode("unsigned"), .width(4)) comparator_1 (
    .a(adder_1_out), .b(4'b0101), .eq(comparator_1_eq));  // open: gt, lt
  Adder #(.width(4)) adder_2 (.a(adder_1_out), .b({2'b00, Instruction[10:9]}), .out(adder_2_out));  // open: cin, cout
  and and_2 (and_2_out, Instruction[11], Instruction[12]);
  Multiplexer #(.enable("false"), .width(3)) multiplexer_1 (
    .in0(Instruction[5:3]), .in1(Instruction[8:6]), .out(multiplexer_1_out), .sel(and_2_out));
  Multiplexer #(.enable("false"), .width(32)) multiplexer_2 (
    .in0(bit_extender_1_out), .in1(negator_1_out), .out(multiplexer_2_out), .sel(and_1_out));
  Multiplexer #(.enable("false"), .width(4)) multiplexer_3 (
    .in0(adder_1_out), .in1(multiplexer_6_out), .out(multiplexer_3_out), .sel(comparator_1_eq));
  Comparator #(.mode("unsigned"), .width(4)) comparator_2 (
    .a(adder_2_out), .b(4'b0110), .gt(comparator_2_gt));  // open: eq, lt
  Adder #(.width(4)) adder_3 (.a(adder_1_out), .b({3'b000, Instruction[9]}), .out(adder_3_out));  // open: cin, cout
  and and_3 (and_3_out, Instruction[10], Instruction[11], Instruction[12]);
  Multiplexer #(.enable("false"), .width(3)) multiplexer_4 (
    .in0(Instruction[2:0]), .in1(Instruction[10:8]), .out(multiplexer_4_out), .sel(Instruction[13]));
  Multiplexer #(.enable("false"), .width(4)) multiplexer_5 (
    .in0(multiplexer_3_out), .in1({Instruction[13:11], 1'b1}), .out(multiplexer_5_out), .sel(Instruction[13]));
  Multiplexer #(.enable("false"), .width(4)) multiplexer_6 (
    .in0(adder_2_out), .in1(adder_3_out), .out(multiplexer_6_out), .sel(comparator_2_gt));
  flags_table flags_table_1 (.codop(bitselector_2_out), .flags(flags_table_1_flags));
  Comparator #(.mode("unsigned"), .width(4)) comparator_3 (
    .a(4'b0110), .b(multiplexer_5_out), .eq(comparator_3_eq));  // open: gt, lt
  or or_1 (or_1_out, and_3_out, Instruction[13]);
  Multiplexer #(.enable("false"), .width(32)) multiplexer_7 (
    .in0(bit_extender_2_out), .in1(multiplexer_2_out), .out(multiplexer_7_out), .sel(Instruction[13]));
  Multiplexer #(.enable("false"), .width(4)) multiplexer_8 (
    .in0(4'b0000), .in1(flags_table_1_flags), .out(Flags_Update_Mask), .sel(Enable));
  Multiplexer #(.enable("false")) multiplexer_9 (.in0(1'b0), .in1(comparator_3_eq), .out(Carry), .sel(Enable));
  Multiplexer #(.enable("false")) multiplexer_10 (.in0(1'b0), .in1(or_1_out), .out(Imm32_Enable), .sel(Enable));
  Multiplexer #(.enable("false"), .width(3)) multiplexer_11 (
    .in0(3'b000), .in1(multiplexer_1_out), .out(Rm), .sel(Enable));
  Multiplexer #(.enable("false"), .width(3)) multiplexer_12 (
    .in0(3'b000), .in1(Instruction[5:3]), .out(Rn), .sel(Enable));
  Multiplexer #(.enable("false"), .width(3)) multiplexer_13 (
    .in0(3'b000), .in1(multiplexer_4_out), .out(Rd), .sel(Enable));
  Multiplexer #(.enable("false"), .width(5)) multiplexer_14 (
    .in0({5{1'b0}}), .in1(Instruction[10:6]), .out(Imm5), .sel(Enable));
  Multiplexer #(.enable("false"), .width(32)) multiplexer_15 (
    .in0({32{1'b0}}), .in1(multiplexer_7_out), .out(Imm32), .sel(Enable));
  Multiplexer #(.enable("false"), .width(4)) multiplexer_16 (
    .in0(4'b0000), .in1(multiplexer_5_out), .out(ALU_Opcode), .sel(Enable));

  // Notes on the sheet:
  //   Note 2: MOV uses RSB ALU opcode with Imm8 reversed so that it is copied to output register
  //   Note: ALU uses Rn register for shifts. Use Rn instead of Rm for shifts (immediate) here too
  //   Note 3: Imm32_Enable forces the use of the immediate for Rm register
  //   Pull output low on Enable = 0
  //   Enable carry for SUB since it is reversed in ALU
  //   ALU will use Imm32 instead of Rm
  //   only ADD and SUB use Rm
endmodule

module flags_table (
  input  [4:0] codop,
  output [3:0] flags
);

  wire and_1_out, and_2_out, and_3_out, not_1_out;

  not not_1 (not_1_out, codop[4]);
  or or_1 (flags[1], not_1_out, codop[2], codop[3]);
  and and_1 (and_1_out, codop[3], codop[2]);
  and and_2 (and_2_out, codop[4], codop[2]);
  and and_3 (and_3_out, codop[4], codop[3]);
  or or_2 (flags[0], and_1_out, and_2_out, and_3_out);

  assign flags[3:2] = 2'b11;
endmodule
